# Fritzing sketch Arduino Bomb (saved by Fritzing 0.9.3b)
breadboards: 1

parts:
  LCM1602_IIC1 = LCM1602 IIC [part_number="LCM1602 IIC" chip_label="LCM1602 IIC" package="DIP (Dual Inline) [THT]"]
  U1 = LCD-16X2 [package=lcd-16x2]
  Onderdeel1 = Arduino Uno (Rev3)
  J1 = Piezo Speaker
  R1 = Resistor [tolerance=±5% resistance=220 package="0603 [SMD]"]
  Keypad4x1 = Keypad Membran 4x4

nets:
  VSS: LCM1602_IIC1.VSS, U1.VSS
  VDD: LCM1602_IIC1.VDD, U1.VDD
  N1: LCM1602_IIC1.V0, U1.VO
  N2: LCM1602_IIC1.RS, U1.RS
  N3: LCM1602_IIC1.RW, U1.R_W
  N4: LCM1602_IIC1.E, U1.E
  N5: LCM1602_IIC1.D0, U1.DB0
  N6: LCM1602_IIC1.D1, U1.DB1
  N7: LCM1602_IIC1.D2, U1.DB2
  N8: LCM1602_IIC1.D3, U1.DB3
  N9: LCM1602_IIC1.D4, U1.DB4
  N10: LCM1602_IIC1.D5, U1.DB5
  N11: LCM1602_IIC1.D6, U1.DB6
  N12: LCM1602_IIC1.D7, U1.DB7
  N13: LCM1602_IIC1.A, U1.A
  N14: LCM1602_IIC1.K, U1.K
  GND: LCM1602_IIC1.GND, Onderdeel1.GND, R1.Pin_1
  VCC: LCM1602_IIC1.VCC, Onderdeel1.5V
  N15: LCM1602_IIC1.SDA, Onderdeel1.A4/SDA
  N16: LCM1602_IIC1.SCL, Onderdeel1.A5/SCL
  N17: Onderdeel1.D8, Keypad4x1.Pin2
  N18: Onderdeel1.D9_PWM, Keypad4x1.Pin1
  N19: Onderdeel1.D10_PWM/SS, J1.pin2
  N20: Onderdeel1.D2, Keypad4x1.Pin8
  N21: Onderdeel1.D3_PWM, Keypad4x1.Pin7
  N22: Onderdeel1.D4, Keypad4x1.Pin6
  N23: Onderdeel1.D5_PWM, Keypad4x1.Pin5
  N24: Onderdeel1.D6_PWM, Keypad4x1.Pin4
  N25: Onderdeel1.D7, Keypad4x1.Pin3
  N26: J1.pin1, R1.Pin_0

custom parts:
  LCM1602 IIC: I2C-Module to use a 1602 or 2004 LCD on with the wire.h libory Serial LCD Modul
  Keypad Membran 4x4: Membrane Keypad 4x4 Matrix

// code stored in the sketch: Untitled2.ino

